# Fritzing sketch BargraphwPot (saved by Fritzing 0.9.3b)
breadboards: 1

parts:
  T3_Vakfı1 = Generic shrouded header - 32 pins [package=THT]
  D1 = LED_BARGRAPH_10 [package=led_bargaph_10]
  U1 = POT [package=alps_pot]

nets:
  N1: T3_Vakfı1.pin2, U1.S
  N2: T3_Vakfı1.pin13, D1.J_A
  N3: T3_Vakfı1.pin17, U1.E
  N4: T3_Vakfı1.pin18, U1.A
  N5: T3_Vakfı1.pin20, D1.I_A
  N6: T3_Vakfı1.pin21, D1.H_A
  N7: T3_Vakfı1.pin22, D1.G_A
  N8: T3_Vakfı1.pin24, D1.F_A
  N9: T3_Vakfı1.pin25, D1.E_A
  N10: T3_Vakfı1.pin26, D1.D_A
  N11: T3_Vakfı1.pin27, D1.C_A
  N12: T3_Vakfı1.pin30, D1.B_A
  N13: T3_Vakfı1.pin31, D1.A_A

custom parts:
  Generic shrouded header - 32 pins: Ülkemizin mühendislik kaynakları kullanılarak geliştirilen Deneyap Kart; güçlü işlemcisi, dayanıklı tasarımı ve çok yönlü giriş/çıkış pinleri ile kullanıcılara Elektronik Programlama, Nesnelerin İnterneti (IoT) ve Yapay Zeka alanlarında başlangıç seviyesinden endüstriyel uygulamalara kadar her seviyede projeyi yapma imkanı sunuyor.
