# Fritzing sketch DCwButtonBC547 (saved by Fritzing 0.9.3b)
breadboards: 1

parts:
  T3_Vakfı1 = Generic shrouded header - 32 pins [package=THT]
  Q1 = NPN-Transistor [part_number=BC547 package="SOT-23 [SMD]"]
  D1 = Rectifier Diode [part_number=1N4001 package="300 mil [THT]"]
  R1 = Resistor [tolerance=±5% resistance=10k package=THT]
  VCC1 = Battery block 9V
  M1 = DC Motor
  S1 = Pushbutton [package="[SMD]"]
  R2 = Resistor [tolerance=±5% resistance=220 package=THT]

nets:
  N1: T3_Vakfı1.pin13, R1.Pin_0
  N2: T3_Vakfı1.pin16, Q1.1, VCC1.-
  N3: T3_Vakfı1.pin17, R2.Pin_0
  N4: T3_Vakfı1.pin18, S1.Pin_3, S1.Pin_4
  N5: T3_Vakfı1.pin31, S1.Pin_1, S1.Pin_2, R2.Pin_1
  N6: Q1.2, D1.anode, M1.pin_2
  N7: Q1.0, R1.Pin_1
  N8: D1.cathode, VCC1.+, M1.pin_1

custom parts:
  Generic shrouded header - 32 pins: Ülkemizin mühendislik kaynakları kullanılarak geliştirilen Deneyap Kart; güçlü işlemcisi, dayanıklı tasarımı ve çok yönlü giriş/çıkış pinleri ile kullanıcılara Elektronik Programlama, Nesnelerin İnterneti (IoT) ve Yapay Zeka alanlarında başlangıç seviyesinden endüstriyel uygulamalara kadar her seviyede projeyi yapma imkanı sunuyor.
