# Fritzing sketch GearDCwPotBC547 (saved by Fritzing 0.9.3b)
breadboards: 1

parts:
  T3_Vakfı1 = Generic shrouded header - 32 pins [package=THT]
  M1 = Getriebemotor
  Q1 = NPN-Transistor [part_number=BC547 package="SOT-23 [SMD]"]
  D1 = Rectifier Diode [part_number=1N4001 package="300 mil [THT]"]
  R1 = Resistor [tolerance=±5% resistance=220 package=THT]
  R2 = Rotary Potentiometer (Small) [maximum_resistance=100kΩ package=THT]

nets:
  N1: T3_Vakfı1.pin2, R2.wiper
  N2: T3_Vakfı1.pin13, R1.Pin_0
  N3: T3_Vakfı1.pin15, M1.pin_2, D1.cathode
  N4: T3_Vakfı1.pin16, Q1.1
  N5: T3_Vakfı1.pin17, R2.leg2
  N6: T3_Vakfı1.pin18, R2.leg1
  N7: M1.pin_1, Q1.2, D1.anode
  N8: Q1.0, R1.Pin_1

custom parts:
  Generic shrouded header - 32 pins: Ülkemizin mühendislik kaynakları kullanılarak geliştirilen Deneyap Kart; güçlü işlemcisi, dayanıklı tasarımı ve çok yönlü giriş/çıkış pinleri ile kullanıcılara Elektronik Programlama, Nesnelerin İnterneti (IoT) ve Yapay Zeka alanlarında başlangıç seviyesinden endüstriyel uygulamalara kadar her seviyede projeyi yapma imkanı sunuyor.
