# Fritzing sketch HC-SR04wLEDsBuzzer (saved by Fritzing 0.9.3b)
breadboards: 1

parts:
  J1 = Piezo Speaker
  LED2 = smd LED [color="Red (633nm)" package="0805 [SMD]"]
  LED4 = smd LED [color="Yellow (595nm)" package="0805 [SMD]"]
  LED6 = smd LED [color="Green (555nm)" package="0805 [SMD]"]
  R1 = Resistor [tolerance=±5% resistance=100 package="1206 [SMD]"]
  R2 = Resistor [tolerance=±5% resistance=100 package="1206 [SMD]"]
  R3 = Resistor [tolerance=±5% resistance=100 package="1206 [SMD]"]
  T3_Vakfı1 = Generic shrouded header - 32 pins [package=THT]
  hc-sr1 = hc-sr04
  R4 = Resistor [tolerance=±5% resistance=100 package="1206 [SMD]"]

nets:
  N1: J1.pin1, R4.Pin_0
  N2: J1.pin2, T3_Vakfı1.pin13
  N3: LED2.cathode, LED4.cathode, LED6.cathode, T3_Vakfı1.pin16, hc-sr1.GND
  N4: LED2.anode, R1.Pin_1
  N5: LED4.anode, R2.Pin_1
  N6: LED6.anode, R3.Pin_0
  N7: R1.Pin_0, T3_Vakfı1.pin12, T3_Vakfı1.pin21
  N8: R2.Pin_0, T3_Vakfı1.pin11
  N9: R3.Pin_1, T3_Vakfı1.pin10
  N10: T3_Vakfı1.pin15, hc-sr1.VCC
  N11: T3_Vakfı1.pin30, hc-sr1.Echo
  N12: T3_Vakfı1.pin31, hc-sr1.Trig
  N13: T3_Vakfı1.pin32, R4.Pin_1

custom parts:
  Generic shrouded header - 32 pins: Ülkemizin mühendislik kaynakları kullanılarak geliştirilen Deneyap Kart; güçlü işlemcisi, dayanıklı tasarımı ve çok yönlü giriş/çıkış pinleri ile kullanıcılara Elektronik Programlama, Nesnelerin İnterneti (IoT) ve Yapay Zeka alanlarında başlangıç seviyesinden endüstriyel uygulamalara kadar her seviyede projeyi yapma imkanı sunuyor.
