# Fritzing sketch LCDwDHT11 (saved by Fritzing 0.9.3b)
breadboards: 1

parts:
  T3_Vakfı1 = Generic shrouded header - 32 pins [package=THT]
  LCD1 = LCD screen
  R2 = Resistor [tolerance=±5% resistance=220 package=THT]
  DHT11_1 = DHT11 module
  U1 = POT [package=alps_pot]

nets:
  N1: T3_Vakfı1.pin10, LCD1.DB4
  N2: T3_Vakfı1.pin11, LCD1.DB5
  N3: T3_Vakfı1.pin12, LCD1.DB6
  N4: T3_Vakfı1.pin13, LCD1.DB7
  N5: T3_Vakfı1.pin15, R2.Pin_0
  N6: T3_Vakfı1.pin16, LCD1.VSS, LCD1.LED-, U1.E
  N7: T3_Vakfı1.pin17, DHT11_1.GND
  VDD: T3_Vakfı1.pin18, LCD1.VDD, DHT11_1.VCC, U1.A
  N8: T3_Vakfı1.pin22, DHT11_1.DATA
  N9: T3_Vakfı1.pin30, LCD1.RS
  N10: T3_Vakfı1.pin31, LCD1.E
  N11: LCD1.V0, U1.S
  N12: LCD1.LED+, R2.Pin_1

custom parts:
  Generic shrouded header - 32 pins: Ülkemizin mühendislik kaynakları kullanılarak geliştirilen Deneyap Kart; güçlü işlemcisi, dayanıklı tasarımı ve çok yönlü giriş/çıkış pinleri ile kullanıcılara Elektronik Programlama, Nesnelerin İnterneti (IoT) ve Yapay Zeka alanlarında başlangıç seviyesinden endüstriyel uygulamalara kadar her seviyede projeyi yapma imkanı sunuyor.
  DHT11 module: https://cdn-learn.adafruit.com/downloads/pdf/dht.pdf DHT11 black pcb module reference by:https://github.com/adafruit/Fritzing-Library/blob/master/parts/DHT11%20Humitidy%20and%20Temperature%20Sensor.fzpz
