# Fritzing sketch 2xLCDwI2C_RTC (saved by Fritzing 0.9.3b)
breadboards: 1

parts:
  LCM1602_IIC1 = LCM1602 IIC [part_number="LCM1602 IIC" chip_label="LCM1602 IIC" package="DIP (Dual Inline) [THT]"]
  T3_Vakfı1 = Generic shrouded header - 32 pins [package=THT]
  U1 = LCD-16X2 [package=lcd-16x2]
  LCM1602_IIC2 = LCM1602 IIC [part_number="LCM1602 IIC" chip_label="LCM1602 IIC" package="DIP (Dual Inline) [THT]"]
  U2 = LCD-16X2 [package=lcd-16x2]
  ZS-042_RTC1 = ZS-042 RTC Module

nets:
  VSS: LCM1602_IIC1.VSS, U1.VSS
  VDD: LCM1602_IIC1.VDD, U1.VDD
  N1: LCM1602_IIC1.V0, U1.VO
  N2: LCM1602_IIC1.RS, U1.RS
  N3: LCM1602_IIC1.RW, U1.R_W
  N4: LCM1602_IIC1.E, U1.E
  N5: LCM1602_IIC1.D0, U1.DB0
  N6: LCM1602_IIC1.D1, U1.DB1
  N7: LCM1602_IIC1.D2, U1.DB2
  N8: LCM1602_IIC1.D3, U1.DB3
  N9: LCM1602_IIC1.D4, U1.DB4
  N10: LCM1602_IIC1.D5, U1.DB5
  N11: LCM1602_IIC1.D6, U1.DB6
  N12: LCM1602_IIC1.D7, U1.DB7
  N13: LCM1602_IIC1.A, U1.A
  N14: LCM1602_IIC1.K, U1.K
  GND: LCM1602_IIC1.GND, T3_Vakfı1.pin16, LCM1602_IIC2.GND, ZS-042_RTC1.GND
  VCC: LCM1602_IIC1.VCC, T3_Vakfı1.pin15, LCM1602_IIC2.VCC
  N15: LCM1602_IIC1.SDA, T3_Vakfı1.pin21, LCM1602_IIC2.SDA, ZS-042_RTC1.SDA
  N16: LCM1602_IIC1.SCL, T3_Vakfı1.pin20, LCM1602_IIC2.SCL, ZS-042_RTC1.SCL
  N17: T3_Vakfı1.pin18, ZS-042_RTC1.VCC
  VSS_2: LCM1602_IIC2.VSS, U2.VSS
  VDD_2: LCM1602_IIC2.VDD, U2.VDD
  N18: LCM1602_IIC2.V0, U2.VO
  N19: LCM1602_IIC2.RS, U2.RS
  N20: LCM1602_IIC2.RW, U2.R_W
  N21: LCM1602_IIC2.E, U2.E
  N22: LCM1602_IIC2.D0, U2.DB0
  N23: LCM1602_IIC2.D1, U2.DB1
  N24: LCM1602_IIC2.D2, U2.DB2
  N25: LCM1602_IIC2.D3, U2.DB3
  N26: LCM1602_IIC2.D4, U2.DB4
  N27: LCM1602_IIC2.D5, U2.DB5
  N28: LCM1602_IIC2.D6, U2.DB6
  N29: LCM1602_IIC2.D7, U2.DB7
  N30: LCM1602_IIC2.A, U2.A
  N31: LCM1602_IIC2.K, U2.K

custom parts:
  LCM1602 IIC: I2C-Module to use a 1602 or 2004 LCD on with the wire.h libory Serial LCD Modul
  Generic shrouded header - 32 pins: Ülkemizin mühendislik kaynakları kullanılarak geliştirilen Deneyap Kart; güçlü işlemcisi, dayanıklı tasarımı ve çok yönlü giriş/çıkış pinleri ile kullanıcılara Elektronik Programlama, Nesnelerin İnterneti (IoT) ve Yapay Zeka alanlarında başlangıç seviyesinden endüstriyel uygulamalara kadar her seviyede projeyi yapma imkanı sunuyor.
