# Fritzing sketch 7segment1digit (saved by Fritzing 0.9.3b)
breadboards: 1

parts:
  T3_Vakfı1 = Generic shrouded header - 32 pins [package=THT]
  7_Segment1 = 7 Segment Display
  R1 = Resistor [tolerance=±5% resistance=220 package=THT]

nets:
  N1: T3_Vakfı1.pin10, 7_Segment1.Segment_B
  N2: T3_Vakfı1.pin11, 7_Segment1.Segment_A
  N3: T3_Vakfı1.pin12, 7_Segment1.Segment_F
  N4: T3_Vakfı1.pin13, 7_Segment1.Segment_G
  N5: T3_Vakfı1.pin17, R1.Pin_0
  N6: T3_Vakfı1.pin26, 7_Segment1.Segment_DP
  N7: T3_Vakfı1.pin27, 7_Segment1.Segment_C
  N8: T3_Vakfı1.pin30, 7_Segment1.Segment_D
  N9: T3_Vakfı1.pin31, 7_Segment1.Segment_E
  N10: 7_Segment1.common_cathode, R1.Pin_1

custom parts:
  Generic shrouded header - 32 pins: Ülkemizin mühendislik kaynakları kullanılarak geliştirilen Deneyap Kart; güçlü işlemcisi, dayanıklı tasarımı ve çok yönlü giriş/çıkış pinleri ile kullanıcılara Elektronik Programlama, Nesnelerin İnterneti (IoT) ve Yapay Zeka alanlarında başlangıç seviyesinden endüstriyel uygulamalara kadar her seviyede projeyi yapma imkanı sunuyor.
