# Fritzing sketch 7segment4digit (saved by Fritzing 0.9.3b)
breadboards: 1

parts:
  T3_Vakfı1 = Generic shrouded header - 32 pins [package=THT]
  HS420561K1 = HS420561K [part_number=HS420561K package="DIP (Dual Inline) [THT]"]

nets:
  N1: T3_Vakfı1.pin10, HS420561K1.pin6
  N2: T3_Vakfı1.pin11, HS420561K1.pin8
  N3: T3_Vakfı1.pin12, HS420561K1.pin_9
  N4: T3_Vakfı1.pin13, HS420561K1.pin_12
  N5: T3_Vakfı1.pin21, HS420561K1.pin3
  N6: T3_Vakfı1.pin22, HS420561K1.pin5
  N7: T3_Vakfı1.pin24, HS420561K1.pin_10
  N8: T3_Vakfı1.pin25, HS420561K1.pin1
  N9: T3_Vakfı1.pin26, HS420561K1.pin2
  N10: T3_Vakfı1.pin27, HS420561K1.pin4
  N11: T3_Vakfı1.pin31, HS420561K1.pin_11

custom parts:
  Generic shrouded header - 32 pins: Ülkemizin mühendislik kaynakları kullanılarak geliştirilen Deneyap Kart; güçlü işlemcisi, dayanıklı tasarımı ve çok yönlü giriş/çıkış pinleri ile kullanıcılara Elektronik Programlama, Nesnelerin İnterneti (IoT) ve Yapay Zeka alanlarında başlangıç seviyesinden endüstriyel uygulamalara kadar her seviyede projeyi yapma imkanı sunuyor.
