# Fritzing sketch RGBwButton (saved by Fritzing 0.9.3b)
breadboards: 1

parts:
  R1 = Resistor [tolerance=±5% resistance=220 package="1206 [SMD]"]
  T3_Vakfı1 = Generic shrouded header - 32 pins [package=THT]
  LED7 = RGB LED (com. cathode, rbg) [package="5 mm [THT]"]
  R3 = Resistor [tolerance=±5% resistance=220 package="1206 [SMD]"]
  R4 = Resistor [tolerance=±5% resistance=220 package="1206 [SMD]"]
  S1 = Pushbutton [package="[SMD]"]
  R5 = Resistor [tolerance=±5% resistance=220 package="1206 [SMD]"]

nets:
  N1: R1.Pin_0, LED7.red_anode
  N2: R1.Pin_1, T3_Vakfı1.pin31
  N3: T3_Vakfı1.pin17, LED7.common_cathode, R5.Pin_1
  N4: T3_Vakfı1.pin18, S1.Pin_3, S1.Pin_4
  N5: T3_Vakfı1.pin26, S1.Pin_1, S1.Pin_2, R5.Pin_0
  N6: T3_Vakfı1.pin27, R3.Pin_1
  N7: T3_Vakfı1.pin30, R4.Pin_1
  N8: LED7.blue_anode, R4.Pin_0
  N9: LED7.green_anode, R3.Pin_0

custom parts:
  Generic shrouded header - 32 pins: Ülkemizin mühendislik kaynakları kullanılarak geliştirilen Deneyap Kart; güçlü işlemcisi, dayanıklı tasarımı ve çok yönlü giriş/çıkış pinleri ile kullanıcılara Elektronik Programlama, Nesnelerin İnterneti (IoT) ve Yapay Zeka alanlarında başlangıç seviyesinden endüstriyel uygulamalara kadar her seviyede projeyi yapma imkanı sunuyor.
